# Fritzing sketch pandora_box_led (saved by Fritzing 0.9.3b)
circuit board: 5.4923cm x 5.88003cm
breadboards: 1

parts:
  MCU = attiny85 [package=dip]
  SW1 = SWITCH_SPDT [package=kps-1290]
  U3 = LIPO-1000mAh [package=lipo-1000]
  SW2 = Pushbutton [package=THT]
  Part1 = ws2812b [package="smd 2812b"]
  R1 = Resistor [tolerance=±5% resistance=220 package="0603 [SMD]"]
  C1 = Electrolytic Capacitor [capacitance=1000μF package="1010 [SMD, electrolytic]"]
  PWR = Header 2 [package=molex-1x2_lock]

nets:
  N1: MCU.Pin_3, R1.Pin_1
  N2: MCU.Pin_4, U3.-, SW2.leg0, Part1.VSS, C1.-, PWR.1
  N3: MCU.Pin_5, SW2.leg1
  N4: MCU.Pin_8, SW1.S, Part1.VDD, C1.+
  N5: SW1.P, U3.+, PWR.2
  N6: Part1.DIN, R1.Pin_0
